# Fritzing sketch GEH KS 28 Uno PCB (saved by Fritzing 0.9.6b)
circuit board: 6.70001cm x 4.51063cm
breadboards: 1

parts:
  U1 = atmega328 [package=dip]
  S1 = Pushbutton [package="[THT]"]
  R1 = Resistor [tolerance=±5% power=0.25 resistance=220 package=THT]
  U2 = Voltage Regulator - 3.3V [package="TO220 [THT]"]
  C1 = Electrolytic Capacitor [capacitance=1µF voltage=35V package="100 mil [THT, electrolytic]"]
  C2 = Electrolytic Capacitor [capacitance=1µF voltage=35V package="100 mil [THT, electrolytic]"]
  XTAL1 = Crystal [frequency="16 Mhz" package=THT]
  LED1 = LED - 5mm [color="Red (633nm)" current=0.030 package="5 mm [THT]"]
  R2 = Resistor [tolerance=±5% power=0.25 resistance=220 package=THT]
  C3 = Ceramic Capacitor [capacitance=10nF voltage=35V package="100 mil [THT, multilayer]"]
  J12 = female pin header, 5 pins [form="♀ (female)"]
  J25 = female pin header, 19 pins [form="♀ (female)"]
  J31 = female pin header, 19 pins [form="♀ (female)"]
  J32 = female pin header, 19 pins [form="♀ (female)"]
  J23 = female pin header, 16 pins [form="♀ (female)"]
  J16 = female pin header, 16 pins [form="♀ (female)"]
  J33 = female pin header, 4 pins [form="♀ (female)"]
  J34 = female pin header, 6 pins [form="♀ (female)"]
  J11 = female pin header, 4 pins [form="♀ (female)"]
  J30 = female pin header, 16 pins [form="♀ (female)"]
  J7 = female pin header, 16 pins [form="♀ (female)"]
  J29 = female pin header, 19 pins [form="♀ (female)"]
  J28 = female pin header, 19 pins [form="♀ (female)"]
  J27 = female pin header, 19 pins [form="♀ (female)"]
  J26 = female pin header, 19 pins [form="♀ (female)"]
  C4 = Capacitor [package=cap-pth-5mm]
  C5 = Capacitor [package=cap-pth-5mm]
  J1 = Screw terminal - 2 pins [package=THT]

nets:
  N1: U1.RESET, S1.Pin_3, R1.Pin_0
  N2: U1.D0_(RX), J12.pin5
  N3: U1.D1_(TX), J12.pin4
  N4: U1.D2, J12.pin3
  N5: U1.D3_(PWM), J12.pin2
  N6: U1.D4, J12.pin1
  N7: U1.VCC, U1.AVCC, U1.AREF, R1.Pin_1, U2.output_voltage, C1.+, C3.1, J25.pin1, J31.pin1, J32.pin1, J23.pin1, J16.pin1, J30.pin1, J7.pin1, J29.pin1, J28.pin1, J27.pin1, J26.pin1
  GND: U1.GND, S1.Pin_1, S1.Pin_2, U2.GND, C1.-, C2.-, LED1.cathode, C3.0, J25.pin19, J31.pin19, J32.pin19, J29.pin19, J28.pin19, J27.pin19, J26.pin19, C4.2, C5.2, J1.pin1
  N8: U1.XLAT1, XTAL1.pin_0, C5.1
  N9: U1.XLAT2, XTAL1.pin_1, C4.1
  N10: U1.D5_(PWM), J11.pin4
  N11: U1.D6_(PWM), J11.pin3
  N12: U1.D7, J11.pin2
  N13: U1.D8, J11.pin1
  N14: U1.D9_(PWM), J33.pin1
  N15: U1.D10_(PWM), J33.pin2
  N16: U1.D11_(PWM), J33.pin3
  N17: U1.D12, J33.pin4
  N18: U1.D13, R2.Pin_0
  N19: U1.A0, J34.pin1
  N20: U1.A1, J34.pin2
  N21: U1.A2, J34.pin3
  N22: U1.A3, J34.pin4
  N23: U1.A4, J34.pin5
  N24: U1.A5, J34.pin6
  N25: U2.input_voltage, C2.+, J1.pin2
  N26: LED1.anode, R2.Pin_1

notes:
  v20210717
  RESET
  VCC
  GND
