# Fritzing sketch TinyPermanente (saved by Fritzing 0.9.6b)
circuit board: 6.62627cm x 2.82971cm
breadboards: 1

parts:
  U1 = attiny85 [package=dip]
  U2 = Voltage Regulator - 5V [package="TO220 [THT]"]
  J1 = Screw terminal - 2 pins [package=THT]
  C1 = Electrolytic Capacitor [capacitance=1µF voltage=35V package="100 mil [THT, electrolytic]"]
  C2 = Electrolytic Capacitor [capacitance=1µF voltage=35V package="100 mil [THT, electrolytic]"]
  J2 = female pin header, 20 pins [form="♀ (female)"]  # not connected
  J3 = female pin header, 20 pins [form="♀ (female)"]  # not connected
  J4 = female pin header, 9 pins [form="♀ (female)"]  # not connected
  J5 = female pin header, 9 pins [form="♀ (female)"]  # not connected
  J6 = female pin header, 9 pins [form="♀ (female)"]  # not connected
  J7 = female pin header, 9 pins [form="♀ (female)"]  # not connected
  J8 = female pin header, 20 pins [form="♀ (female)"]  # not connected
  J9 = female pin header, 20 pins [form="♀ (female)"]  # not connected
  J10 = female pin header, 20 pins [form="♀ (female)"]  # not connected
  J11 = female pin header, 20 pins [form="♀ (female)"]  # not connected

nets:
  N1: U1.Pin_4, U2.GND, J1.pin1, C1.-, C2.-
  N2: U1.Pin_8, U2.output_voltage, C2.+
  N3: U2.input_voltage, J1.pin2, C1.+
